// Logisim project project (2).circ as structural Verilog: 13 circuits, main circuit mod 10 counter
module mod_10_counter (
  input  in_1,
  input  in_2,
  output out_3,
  output out_4,
  output out_5,
  output out_6
);

  wire and_1_out, and_2_out, and_3_out, and_4_out, j_k_ff_2_qn, j_k_ff_4_qn;

  and and_1 (and_1_out, out_6, out_5);
  and and_2 (and_2_out, j_k_ff_2_qn, out_6);
  J_K_Flip_Flop #(.trigger("falling")) j_k_ff_1 (
    .J(1'b1), .clk(in_2), .K(1'b1), .Q(out_6), .reset(in_1));  // open: Qn, preset, en
  J_K_Flip_Flop #(.trigger("falling")) j_k_ff_2 (
    .J(and_3_out), .clk(in_2), .K(and_1_out), .Q(out_5), .Qn(j_k_ff_2_qn), .reset(in_1));  // open: preset, en
  and and_3 (and_3_out, out_6, j_k_ff_4_qn);
  J_K_Flip_Flop #(.trigger("falling")) j_k_ff_3 (
    .J(and_1_out), .clk(in_2), .K(and_1_out), .Q(out_4), .reset(in_1));  // open: Qn, preset, en
  and and_4 (and_4_out, out_4, and_1_out);
  J_K_Flip_Flop #(.trigger("falling")) j_k_ff_4 (
    .J(and_4_out), .clk(in_2), .K(and_2_out), .Q(out_3), .Qn(j_k_ff_4_qn), .reset(in_1));  // open: preset, en

  // Notes on the sheet:
  //   cd
  //   c'd
  //   d
  //   c
  //   a'd
  //   b
  //   bcd
  //   a
endmodule

module mod_6_counter (
  input  in_1,
  input  in_2,
  output out_3,
  output out_4,
  output out_5
);

  wire and_1_out, and_2_out, and_3_out, j_k_ff_2_qn, j_k_ff_3_qn;

  J_K_Flip_Flop #(.trigger("falling")) j_k_ff_1 (
    .J(1'b1), .clk(in_2), .K(1'b1), .Q(out_5), .reset(in_1));  // open: Qn, preset, en
  and and_1 (and_1_out, j_k_ff_3_qn, out_5);
  J_K_Flip_Flop #(.trigger("falling")) j_k_ff_2 (
    .J(and_1_out), .clk(in_2), .K(and_2_out), .Q(out_4), .Qn(j_k_ff_2_qn), .reset(in_1));  // open: preset, en
  and and_2 (and_2_out, out_4, out_5);
  and and_3 (and_3_out, j_k_ff_2_qn, out_5);
  J_K_Flip_Flop #(.trigger("falling")) j_k_ff_3 (
    .J(and_2_out), .clk(in_2), .K(and_3_out), .Q(out_3), .Qn(j_k_ff_3_qn), .reset(in_1));  // open: preset, en

  // Notes on the sheet:
  //   c
  //   b
  //   a
endmodule

module bcd_to_seven_segment_decoder (
  input  in_1,
  input  in_2,
  input  in_3,
  input  in_4,
  output out_5,
  output out_6,
  output c,
  output out_8,
  output out_9,
  output out_10,
  output out_11
);

  wire decoder_1_out0, decoder_1_out1, decoder_1_out2, decoder_1_out3, decoder_1_out4, decoder_1_out5,
       decoder_1_out6, decoder_1_out7, decoder_1_out9;

  Decoder #(.select(4)) decoder_1 (
    .out0(decoder_1_out0), .out1(decoder_1_out1), .out2(decoder_1_out2), .out3(decoder_1_out3),
    .out4(decoder_1_out4), .out5(decoder_1_out5), .out6(decoder_1_out6), .out7(decoder_1_out7),
    .out9(decoder_1_out9), .sel({in_1, in_2, in_3, in_4}), .en(1'b1));  // open: out8, out10, out11, out12, out13, out14, out15
  or or_1 (out_5, decoder_1_out1, decoder_1_out4);
  or or_2 (out_6, decoder_1_out5, decoder_1_out6);
  or or_3 (c, decoder_1_out2, decoder_1_out2, decoder_1_out2);
  or or_4 (out_8, decoder_1_out1, decoder_1_out4, decoder_1_out7);
  or or_5 (out_9, decoder_1_out1, decoder_1_out3, decoder_1_out4, decoder_1_out5, decoder_1_out7, decoder_1_out9);
  or or_6 (out_10, decoder_1_out1, decoder_1_out2, decoder_1_out3, decoder_1_out7);
  or or_7 (out_11, decoder_1_out0, decoder_1_out1, decoder_1_out7);
  _7_Segment_Display #(.active("false")) u_7_segment_display_1 (
    .g(out_11), .f(out_10), .a(out_5), .b(out_6), .e(out_9), .d(out_8), .c(c), .dp(1'b1));

  // Notes on the sheet:
  //   a
  //   b
  //   d
  //   e
  //   f
  //   g
endmodule

module main (
  input  START
);

  wire and_1_out, button_1_out, button_2_out, clock_1_out, comparator_1_out_3, comparator_1_out_4,
       comparator_1_out_5, comparator_1_out_6, comparator_1_out_7, comparator_1_out_8, comparator_1_out_9,
       not_1_out, or_1_out;
  wire [3:0] simple_display_lower_1_out_2, simple_display_lower_1_out_3, simple_display_lower_1_out_4,
       simple_display_lower_1_out_5, simple_display_lower_1_out_6, simple_display_lower_1_out_7,
       simple_display_upper_1_out_2, simple_display_upper_1_out_3, simple_display_upper_1_out_4,
       simple_display_upper_1_out_5, simple_display_upper_1_out_6, simple_display_upper_1_out_7,
       timer_for_lower_display_1_out_4, timer_for_lower_display_1_out_5, timer_for_lower_display_1_out_6,
       timer_for_lower_display_1_out_7, timer_for_lower_display_1_out_8, timer_for_lower_display_1_out_9,
       timer_for_lower_display_2_out_4, timer_for_lower_display_2_out_5, timer_for_lower_display_2_out_6,
       timer_for_lower_display_2_out_7, timer_for_lower_display_2_out_8, timer_for_lower_display_2_out_9,
       timer_for_lower_display_3_out_4, timer_for_lower_display_3_out_5, timer_for_lower_display_3_out_6,
       timer_for_lower_display_3_out_7, timer_for_lower_display_3_out_8, timer_for_lower_display_3_out_9,
       timer_for_lower_display_4_out_4, timer_for_lower_display_4_out_5, timer_for_lower_display_4_out_6,
       timer_for_lower_display_4_out_7, timer_for_lower_display_4_out_8, timer_for_lower_display_4_out_9,
       timer_for_lower_display_5_out_4, timer_for_lower_display_5_out_5, timer_for_lower_display_5_out_6,
       timer_for_lower_display_5_out_7, timer_for_lower_display_5_out_8, timer_for_lower_display_5_out_9,
       timer_for_lower_display_6_out_4, timer_for_lower_display_6_out_5, timer_for_lower_display_6_out_6,
       timer_for_lower_display_6_out_7, timer_for_lower_display_6_out_8, timer_for_lower_display_6_out_9,
       timer_for_upperr_display_1_out_3, timer_for_upperr_display_1_out_4, timer_for_upperr_display_1_out_5,
       timer_for_upperr_display_1_out_6, timer_for_upperr_display_1_out_7, timer_for_upperr_display_1_out_8,
       timer_for_upperr_display_2_out_3, timer_for_upperr_display_2_out_4, timer_for_upperr_display_2_out_5,
       timer_for_upperr_display_2_out_6, timer_for_upperr_display_2_out_7, timer_for_upperr_display_2_out_8,
       timer_for_upperr_display_3_out_3, timer_for_upperr_display_3_out_4, timer_for_upperr_display_3_out_5,
       timer_for_upperr_display_3_out_6, timer_for_upperr_display_3_out_7, timer_for_upperr_display_3_out_8,
       timer_for_upperr_display_4_out_3, timer_for_upperr_display_4_out_4, timer_for_upperr_display_4_out_5,
       timer_for_upperr_display_4_out_6, timer_for_upperr_display_4_out_7, timer_for_upperr_display_4_out_8,
       timer_for_upperr_display_5_out_3, timer_for_upperr_display_5_out_4, timer_for_upperr_display_5_out_5,
       timer_for_upperr_display_5_out_6, timer_for_upperr_display_5_out_7, timer_for_upperr_display_5_out_8,
       timer_for_upperr_display_6_out_3, timer_for_upperr_display_6_out_4, timer_for_upperr_display_6_out_5,
       timer_for_upperr_display_6_out_6, timer_for_upperr_display_6_out_7, timer_for_upperr_display_6_out_8;
  wire [23:0] n16_bit_comparator_1_out_6, timer_for_lower_display_1_out_3, timer_for_lower_display_2_out_3,
       timer_for_lower_display_3_out_3, timer_for_lower_display_4_out_3, timer_for_lower_display_5_out_3;

  _7_Segment_Display #(.active("false")) u_7_segment_display_1 (
    .g(timer_for_upperr_display_1_out_4[3]), .f(timer_for_upperr_display_1_out_4[2]),
    .a(timer_for_upperr_display_1_out_4[1]), .b(timer_for_upperr_display_1_out_4[0]),
    .e(timer_for_lower_display_1_out_5[3]), .d(timer_for_lower_display_1_out_5[2]),
    .c(timer_for_lower_display_1_out_5[1]), .dp(timer_for_lower_display_1_out_5[0]));
  _7_Segment_Display #(.active("false")) u_7_segment_display_2 (
    .g(timer_for_upperr_display_2_out_4[3]), .f(timer_for_upperr_display_2_out_4[2]),
    .a(timer_for_upperr_display_2_out_4[1]), .b(timer_for_upperr_display_2_out_4[0]),
    .e(timer_for_lower_display_2_out_5[3]), .d(timer_for_lower_display_2_out_5[2]),
    .c(timer_for_lower_display_2_out_5[1]), .dp(timer_for_lower_display_2_out_5[0]));
  _7_Segment_Display #(.active("false")) u_7_segment_display_3 (
    .g(timer_for_upperr_display_3_out_4[3]), .f(timer_for_upperr_display_3_out_4[2]),
    .a(timer_for_upperr_display_3_out_4[1]), .b(timer_for_upperr_display_3_out_4[0]),
    .e(timer_for_lower_display_3_out_5[3]), .d(timer_for_lower_display_3_out_5[2]),
    .c(timer_for_lower_display_3_out_5[1]), .dp(timer_for_lower_display_3_out_5[0]));
  _7_Segment_Display #(.active("false")) u_7_segment_display_4 (
    .g(timer_for_upperr_display_4_out_4[3]), .f(timer_for_upperr_display_4_out_4[2]),
    .a(timer_for_upperr_display_4_out_4[1]), .b(timer_for_upperr_display_4_out_4[0]),
    .e(timer_for_lower_display_4_out_5[3]), .d(timer_for_lower_display_4_out_5[2]),
    .c(timer_for_lower_display_4_out_5[1]), .dp(timer_for_lower_display_4_out_5[0]));
  _7_Segment_Display #(.active("false")) u_7_segment_display_5 (
    .g(timer_for_upperr_display_5_out_4[3]), .f(timer_for_upperr_display_5_out_4[2]),
    .a(timer_for_upperr_display_5_out_4[1]), .b(timer_for_upperr_display_5_out_4[0]),
    .e(timer_for_lower_display_5_out_5[3]), .d(timer_for_lower_display_5_out_5[2]),
    .c(timer_for_lower_display_5_out_5[1]), .dp(timer_for_lower_display_5_out_5[0]));
  _7_Segment_Display #(.active("false")) u_7_segment_display_6 (
    .g(timer_for_upperr_display_1_out_5[3]), .f(timer_for_upperr_display_1_out_5[2]),
    .a(timer_for_upperr_display_1_out_5[1]), .b(timer_for_upperr_display_1_out_5[0]),
    .e(timer_for_lower_display_1_out_6[3]), .d(timer_for_lower_display_1_out_6[2]),
    .c(timer_for_lower_display_1_out_6[1]), .dp(timer_for_lower_display_1_out_6[0]));
  _7_Segment_Display #(.active("false")) u_7_segment_display_7 (
    .g(timer_for_upperr_display_2_out_5[3]), .f(timer_for_upperr_display_2_out_5[2]),
    .a(timer_for_upperr_display_2_out_5[1]), .b(timer_for_upperr_display_2_out_5[0]),
    .e(timer_for_lower_display_2_out_6[3]), .d(timer_for_lower_display_2_out_6[2]),
    .c(timer_for_lower_display_2_out_6[1]), .dp(timer_for_lower_display_2_out_6[0]));
  _7_Segment_Display #(.active("false")) u_7_segment_display_8 (
    .g(timer_for_upperr_display_3_out_5[3]), .f(timer_for_upperr_display_3_out_5[2]),
    .a(timer_for_upperr_display_3_out_5[1]), .b(timer_for_upperr_display_3_out_5[0]),
    .e(timer_for_lower_display_3_out_6[3]), .d(timer_for_lower_display_3_out_6[2]),
    .c(timer_for_lower_display_3_out_6[1]), .dp(timer_for_lower_display_3_out_6[0]));
  _7_Segment_Display #(.active("false")) u_7_segment_display_9 (
    .g(timer_for_upperr_display_4_out_5[3]), .f(timer_for_upperr_display_4_out_5[2]),
    .a(timer_for_upperr_display_4_out_5[1]), .b(timer_for_upperr_display_4_out_5[0]),
    .e(timer_for_lower_display_4_out_6[3]), .d(timer_for_lower_display_4_out_6[2]),
    .c(timer_for_lower_display_4_out_6[1]), .dp(timer_for_lower_display_4_out_6[0]));
  _7_Segment_Display #(.active("false")) u_7_segment_display_10 (
    .g(timer_for_upperr_display_5_out_5[3]), .f(timer_for_upperr_display_5_out_5[2]),
    .a(timer_for_upperr_display_5_out_5[1]), .b(timer_for_upperr_display_5_out_5[0]),
    .e(timer_for_lower_display_5_out_6[3]), .d(timer_for_lower_display_5_out_6[2]),
    .c(timer_for_lower_display_5_out_6[1]), .dp(timer_for_lower_display_5_out_6[0]));
  _7_Segment_Display #(.active("false")) u_7_segment_display_11 (
    .g(timer_for_upperr_display_1_out_6[3]), .f(timer_for_upperr_display_1_out_6[2]),
    .a(timer_for_upperr_display_1_out_6[1]), .b(timer_for_upperr_display_1_out_6[0]),
    .e(timer_for_lower_display_1_out_7[3]), .d(timer_for_lower_display_1_out_7[2]),
    .c(timer_for_lower_display_1_out_7[1]), .dp(timer_for_lower_display_1_out_7[0]));
  _7_Segment_Display #(.active("false")) u_7_segment_display_12 (
    .g(timer_for_upperr_display_2_out_6[3]), .f(timer_for_upperr_display_2_out_6[2]),
    .a(timer_for_upperr_display_2_out_6[1]), .b(timer_for_upperr_display_2_out_6[0]),
    .e(timer_for_lower_display_2_out_7[3]), .d(timer_for_lower_display_2_out_7[2]),
    .c(timer_for_lower_display_2_out_7[1]), .dp(timer_for_lower_display_2_out_7[0]));
  _7_Segment_Display #(.active("false")) u_7_segment_display_13 (
    .g(timer_for_upperr_display_3_out_6[3]), .f(timer_for_upperr_display_3_out_6[2]),
    .a(timer_for_upperr_display_3_out_6[1]), .b(timer_for_upperr_display_3_out_6[0]),
    .e(timer_for_lower_display_3_out_7[3]), .d(timer_for_lower_display_3_out_7[2]),
    .c(timer_for_lower_display_3_out_7[1]), .dp(timer_for_lower_display_3_out_7[0]));
  _7_Segment_Display #(.active("false")) u_7_segment_display_14 (
    .g(timer_for_upperr_display_4_out_6[3]), .f(timer_for_upperr_display_4_out_6[2]),
    .a(timer_for_upperr_display_4_out_6[1]), .b(timer_for_upperr_display_4_out_6[0]),
    .e(timer_for_lower_display_4_out_7[3]), .d(timer_for_lower_display_4_out_7[2]),
    .c(timer_for_lower_display_4_out_7[1]), .dp(timer_for_lower_display_4_out_7[0]));
  _7_Segment_Display #(.active("false")) u_7_segment_display_15 (
    .g(timer_for_upperr_display_5_out_6[3]), .f(timer_for_upperr_display_5_out_6[2]),
    .a(timer_for_upperr_display_5_out_6[1]), .b(timer_for_upperr_display_5_out_6[0]),
    .e(timer_for_lower_display_5_out_7[3]), .d(timer_for_lower_display_5_out_7[2]),
    .c(timer_for_lower_display_5_out_7[1]), .dp(timer_for_lower_display_5_out_7[0]));
  _7_Segment_Display #(.active("false")) u_7_segment_display_16 (
    .g(timer_for_upperr_display_1_out_7[3]), .f(timer_for_upperr_display_1_out_7[2]),
    .a(timer_for_upperr_display_1_out_7[1]), .b(timer_for_upperr_display_1_out_7[0]),
    .e(timer_for_lower_display_1_out_8[3]), .d(timer_for_lower_display_1_out_8[2]),
    .c(timer_for_lower_display_1_out_8[1]), .dp(timer_for_lower_display_1_out_8[0]));
  _7_Segment_Display #(.active("false")) u_7_segment_display_17 (
    .g(timer_for_upperr_display_2_out_7[3]), .f(timer_for_upperr_display_2_out_7[2]),
    .a(timer_for_upperr_display_2_out_7[1]), .b(timer_for_upperr_display_2_out_7[0]),
    .e(timer_for_lower_display_2_out_8[3]), .d(timer_for_lower_display_2_out_8[2]),
    .c(timer_for_lower_display_2_out_8[1]), .dp(timer_for_lower_display_2_out_8[0]));
  _7_Segment_Display #(.active("false")) u_7_segment_display_18 (
    .g(timer_for_upperr_display_3_out_7[3]), .f(timer_for_upperr_display_3_out_7[2]),
    .a(timer_for_upperr_display_3_out_7[1]), .b(timer_for_upperr_display_3_out_7[0]),
    .e(timer_for_lower_display_3_out_8[3]), .d(timer_for_lower_display_3_out_8[2]),
    .c(timer_for_lower_display_3_out_8[1]), .dp(timer_for_lower_display_3_out_8[0]));
  _7_Segment_Display #(.active("false")) u_7_segment_display_19 (
    .g(timer_for_upperr_display_4_out_7[3]), .f(timer_for_upperr_display_4_out_7[2]),
    .a(timer_for_upperr_display_4_out_7[1]), .b(timer_for_upperr_display_4_out_7[0]),
    .e(timer_for_lower_display_4_out_8[3]), .d(timer_for_lower_display_4_out_8[2]),
    .c(timer_for_lower_display_4_out_8[1]), .dp(timer_for_lower_display_4_out_8[0]));
  _7_Segment_Display #(.active("false")) u_7_segment_display_20 (
    .g(timer_for_upperr_display_5_out_7[3]), .f(timer_for_upperr_display_5_out_7[2]),
    .a(timer_for_upperr_display_5_out_7[1]), .b(timer_for_upperr_display_5_out_7[0]),
    .e(timer_for_lower_display_5_out_8[3]), .d(timer_for_lower_display_5_out_8[2]),
    .c(timer_for_lower_display_5_out_8[1]), .dp(timer_for_lower_display_5_out_8[0]));
  _7_Segment_Display #(.active("false")) u_7_segment_display_21 (
    .g(timer_for_upperr_display_1_out_8[3]), .f(timer_for_upperr_display_1_out_8[2]),
    .a(timer_for_upperr_display_1_out_8[1]), .b(timer_for_upperr_display_1_out_8[0]),
    .e(timer_for_lower_display_1_out_9[3]), .d(timer_for_lower_display_1_out_9[2]),
    .c(timer_for_lower_display_1_out_9[1]), .dp(timer_for_lower_display_1_out_9[0]));
  _7_Segment_Display #(.active("false")) u_7_segment_display_22 (
    .g(timer_for_upperr_display_2_out_8[3]), .f(timer_for_upperr_display_2_out_8[2]),
    .a(timer_for_upperr_display_2_out_8[1]), .b(timer_for_upperr_display_2_out_8[0]),
    .e(timer_for_lower_display_2_out_9[3]), .d(timer_for_lower_display_2_out_9[2]),
    .c(timer_for_lower_display_2_out_9[1]), .dp(timer_for_lower_display_2_out_9[0]));
  _7_Segment_Display #(.active("false")) u_7_segment_display_23 (
    .g(timer_for_upperr_display_3_out_8[3]), .f(timer_for_upperr_display_3_out_8[2]),
    .a(timer_for_upperr_display_3_out_8[1]), .b(timer_for_upperr_display_3_out_8[0]),
    .e(timer_for_lower_display_3_out_9[3]), .d(timer_for_lower_display_3_out_9[2]),
    .c(timer_for_lower_display_3_out_9[1]), .dp(timer_for_lower_display_3_out_9[0]));
  _7_Segment_Display #(.active("false")) u_7_segment_display_24 (
    .g(timer_for_upperr_display_4_out_8[3]), .f(timer_for_upperr_display_4_out_8[2]),
    .a(timer_for_upperr_display_4_out_8[1]), .b(timer_for_upperr_display_4_out_8[0]),
    .e(timer_for_lower_display_4_out_9[3]), .d(timer_for_lower_display_4_out_9[2]),
    .c(timer_for_lower_display_4_out_9[1]), .dp(timer_for_lower_display_4_out_9[0]));
  _7_Segment_Display #(.active("false")) u_7_segment_display_25 (
    .g(timer_for_upperr_display_5_out_8[3]), .f(timer_for_upperr_display_5_out_8[2]),
    .a(timer_for_upperr_display_5_out_8[1]), .b(timer_for_upperr_display_5_out_8[0]),
    .e(timer_for_lower_display_5_out_9[3]), .d(timer_for_lower_display_5_out_9[2]),
    .c(timer_for_lower_display_5_out_9[1]), .dp(timer_for_lower_display_5_out_9[0]));
  timer_for_upperr_display timer_for_upperr_display_1 (
    .in_1(button_1_out), .in_2(comparator_1_out_3), .out_4(timer_for_upperr_display_1_out_4),
    .out_5(timer_for_upperr_display_1_out_5), .out_6(timer_for_upperr_display_1_out_6),
    .out_7(timer_for_upperr_display_1_out_7), .out_8(timer_for_upperr_display_1_out_8),
    .out_3(timer_for_upperr_display_1_out_3));
  _7_Segment_Display #(.active("false")) u_7_segment_display_26 (
    .g(timer_for_upperr_display_1_out_3[3]), .f(timer_for_upperr_display_1_out_3[2]),
    .a(timer_for_upperr_display_1_out_3[1]), .b(timer_for_upperr_display_1_out_3[0]),
    .e(timer_for_lower_display_1_out_4[3]), .d(timer_for_lower_display_1_out_4[2]),
    .c(timer_for_lower_display_1_out_4[1]), .dp(timer_for_lower_display_1_out_4[0]));
  timer_for_lower_display timer_for_lower_display_1 (
    .out_5(timer_for_lower_display_1_out_5), .out_6(timer_for_lower_display_1_out_6),
    .out_7(timer_for_lower_display_1_out_7), .out_8(timer_for_lower_display_1_out_8),
    .out_9(timer_for_lower_display_1_out_9), .out_4(timer_for_lower_display_1_out_4), .in_1(button_1_out),
    .out_3(timer_for_lower_display_1_out_3), .in_2(comparator_1_out_3));
  timer_for_upperr_display timer_for_upperr_display_2 (
    .in_1(button_1_out), .in_2(comparator_1_out_4), .out_4(timer_for_upperr_display_2_out_4),
    .out_5(timer_for_upperr_display_2_out_5), .out_6(timer_for_upperr_display_2_out_6),
    .out_7(timer_for_upperr_display_2_out_7), .out_8(timer_for_upperr_display_2_out_8),
    .out_3(timer_for_upperr_display_2_out_3));
  _7_Segment_Display #(.active("false")) u_7_segment_display_27 (
    .g(timer_for_upperr_display_2_out_3[3]), .f(timer_for_upperr_display_2_out_3[2]),
    .a(timer_for_upperr_display_2_out_3[1]), .b(timer_for_upperr_display_2_out_3[0]),
    .e(timer_for_lower_display_2_out_4[3]), .d(timer_for_lower_display_2_out_4[2]),
    .c(timer_for_lower_display_2_out_4[1]), .dp(timer_for_lower_display_2_out_4[0]));
  timer_for_lower_display timer_for_lower_display_2 (
    .out_5(timer_for_lower_display_2_out_5), .out_6(timer_for_lower_display_2_out_6),
    .out_7(timer_for_lower_display_2_out_7), .out_8(timer_for_lower_display_2_out_8),
    .out_9(timer_for_lower_display_2_out_9), .out_4(timer_for_lower_display_2_out_4), .in_1(button_1_out),
    .out_3(timer_for_lower_display_2_out_3), .in_2(comparator_1_out_4));
  timer_for_upperr_display timer_for_upperr_display_3 (
    .in_1(button_1_out), .in_2(comparator_1_out_5), .out_4(timer_for_upperr_display_3_out_4),
    .out_5(timer_for_upperr_display_3_out_5), .out_6(timer_for_upperr_display_3_out_6),
    .out_7(timer_for_upperr_display_3_out_7), .out_8(timer_for_upperr_display_3_out_8),
    .out_3(timer_for_upperr_display_3_out_3));
  _7_Segment_Display #(.active("false")) u_7_segment_display_28 (
    .g(timer_for_upperr_display_3_out_3[3]), .f(timer_for_upperr_display_3_out_3[2]),
    .a(timer_for_upperr_display_3_out_3[1]), .b(timer_for_upperr_display_3_out_3[0]),
    .e(timer_for_lower_display_3_out_4[3]), .d(timer_for_lower_display_3_out_4[2]),
    .c(timer_for_lower_display_3_out_4[1]), .dp(timer_for_lower_display_3_out_4[0]));
  timer_for_lower_display timer_for_lower_display_3 (
    .out_5(timer_for_lower_display_3_out_5), .out_6(timer_for_lower_display_3_out_6),
    .out_7(timer_for_lower_display_3_out_7), .out_8(timer_for_lower_display_3_out_8),
    .out_9(timer_for_lower_display_3_out_9), .out_4(timer_for_lower_display_3_out_4), .in_1(button_1_out),
    .out_3(timer_for_lower_display_3_out_3), .in_2(comparator_1_out_5));
  timer_for_upperr_display timer_for_upperr_display_4 (
    .in_1(button_1_out), .in_2(comparator_1_out_6), .out_4(timer_for_upperr_display_4_out_4),
    .out_5(timer_for_upperr_display_4_out_5), .out_6(timer_for_upperr_display_4_out_6),
    .out_7(timer_for_upperr_display_4_out_7), .out_8(timer_for_upperr_display_4_out_8),
    .out_3(timer_for_upperr_display_4_out_3));
  _7_Segment_Display #(.active("false")) u_7_segment_display_29 (
    .g(timer_for_upperr_display_4_out_3[3]), .f(timer_for_upperr_display_4_out_3[2]),
    .a(timer_for_upperr_display_4_out_3[1]), .b(timer_for_upperr_display_4_out_3[0]),
    .e(timer_for_lower_display_4_out_4[3]), .d(timer_for_lower_display_4_out_4[2]),
    .c(timer_for_lower_display_4_out_4[1]), .dp(timer_for_lower_display_4_out_4[0]));
  timer_for_lower_display timer_for_lower_display_4 (
    .out_5(timer_for_lower_display_4_out_5), .out_6(timer_for_lower_display_4_out_6),
    .out_7(timer_for_lower_display_4_out_7), .out_8(timer_for_lower_display_4_out_8),
    .out_9(timer_for_lower_display_4_out_9), .out_4(timer_for_lower_display_4_out_4), .in_1(button_1_out),
    .out_3(timer_for_lower_display_4_out_3), .in_2(comparator_1_out_6));
  timer_for_upperr_display timer_for_upperr_display_5 (
    .in_1(button_1_out), .in_2(comparator_1_out_7), .out_4(timer_for_upperr_display_5_out_4),
    .out_5(timer_for_upperr_display_5_out_5), .out_6(timer_for_upperr_display_5_out_6),
    .out_7(timer_for_upperr_display_5_out_7), .out_8(timer_for_upperr_display_5_out_8),
    .out_3(timer_for_upperr_display_5_out_3));
  _7_Segment_Display #(.active("false")) u_7_segment_display_30 (
    .g(timer_for_upperr_display_5_out_3[3]), .f(timer_for_upperr_display_5_out_3[2]),
    .a(timer_for_upperr_display_5_out_3[1]), .b(timer_for_upperr_display_5_out_3[0]),
    .e(timer_for_lower_display_5_out_4[3]), .d(timer_for_lower_display_5_out_4[2]),
    .c(timer_for_lower_display_5_out_4[1]), .dp(timer_for_lower_display_5_out_4[0]));
  timer_for_lower_display timer_for_lower_display_5 (
    .out_5(timer_for_lower_display_5_out_5), .out_6(timer_for_lower_display_5_out_6),
    .out_7(timer_for_lower_display_5_out_7), .out_8(timer_for_lower_display_5_out_8),
    .out_9(timer_for_lower_display_5_out_9), .out_4(timer_for_lower_display_5_out_4), .in_1(button_1_out),
    .out_3(timer_for_lower_display_5_out_3), .in_2(comparator_1_out_7));
  _7_Segment_Display #(.active("false")) u_7_segment_display_31 (
    .g(timer_for_upperr_display_6_out_4[3]), .f(timer_for_upperr_display_6_out_4[2]),
    .a(timer_for_upperr_display_6_out_4[1]), .b(timer_for_upperr_display_6_out_4[0]),
    .e(timer_for_lower_display_6_out_5[3]), .d(timer_for_lower_display_6_out_5[2]),
    .c(timer_for_lower_display_6_out_5[1]), .dp(timer_for_lower_display_6_out_5[0]));
  _7_Segment_Display #(.active("false")) u_7_segment_display_32 (
    .g(timer_for_upperr_display_6_out_5[3]), .f(timer_for_upperr_display_6_out_5[2]),
    .a(timer_for_upperr_display_6_out_5[1]), .b(timer_for_upperr_display_6_out_5[0]),
    .e(timer_for_lower_display_6_out_6[3]), .d(timer_for_lower_display_6_out_6[2]),
    .c(timer_for_lower_display_6_out_6[1]), .dp(timer_for_lower_display_6_out_6[0]));
  _7_Segment_Display #(.active("false")) u_7_segment_display_33 (
    .g(simple_display_upper_1_out_3[3]), .f(simple_display_upper_1_out_3[2]),
    .a(simple_display_upper_1_out_3[1]), .b(simple_display_upper_1_out_3[0]),
    .e(simple_display_lower_1_out_3[3]), .d(simple_display_lower_1_out_3[2]),
    .c(simple_display_lower_1_out_3[1]), .dp(simple_display_lower_1_out_3[0]));
  _7_Segment_Display #(.active("false")) u_7_segment_display_34 (
    .g(timer_for_upperr_display_6_out_6[3]), .f(timer_for_upperr_display_6_out_6[2]),
    .a(timer_for_upperr_display_6_out_6[1]), .b(timer_for_upperr_display_6_out_6[0]),
    .e(timer_for_lower_display_6_out_7[3]), .d(timer_for_lower_display_6_out_7[2]),
    .c(timer_for_lower_display_6_out_7[1]), .dp(timer_for_lower_display_6_out_7[0]));
  comparator comparator_1 (
    .in_1(and_1_out), .out_3(comparator_1_out_3), .out_4(comparator_1_out_4), .out_5(comparator_1_out_5),
    .out_6(comparator_1_out_6), .out_7(comparator_1_out_7), .in_2(button_2_out), .out_9(comparator_1_out_9),
    .out_8(comparator_1_out_8));
  _16_bit_comparator u_16_bit_comparator_1 (
    .in_1(timer_for_lower_display_1_out_3), .in_2(timer_for_lower_display_2_out_3),
    .in_3(timer_for_lower_display_3_out_3), .in_4(timer_for_lower_display_4_out_3),
    .in_5(timer_for_lower_display_5_out_3), .out_6(n16_bit_comparator_1_out_6));
  _7_Segment_Display #(.active("false")) u_7_segment_display_35 (
    .g(simple_display_upper_1_out_4[3]), .f(simple_display_upper_1_out_4[2]),
    .a(simple_display_upper_1_out_4[1]), .b(simple_display_upper_1_out_4[0]),
    .e(simple_display_lower_1_out_4[3]), .d(simple_display_lower_1_out_4[2]),
    .c(simple_display_lower_1_out_4[1]), .dp(simple_display_lower_1_out_4[0]));
  _7_Segment_Display #(.active("false")) u_7_segment_display_36 (
    .g(timer_for_upperr_display_6_out_7[3]), .f(timer_for_upperr_display_6_out_7[2]),
    .a(timer_for_upperr_display_6_out_7[1]), .b(timer_for_upperr_display_6_out_7[0]),
    .e(timer_for_lower_display_6_out_8[3]), .d(timer_for_lower_display_6_out_8[2]),
    .c(timer_for_lower_display_6_out_8[1]), .dp(timer_for_lower_display_6_out_8[0]));
  _7_Segment_Display #(.active("false")) u_7_segment_display_37 (
    .g(simple_display_upper_1_out_5[3]), .f(simple_display_upper_1_out_5[2]),
    .a(simple_display_upper_1_out_5[1]), .b(simple_display_upper_1_out_5[0]),
    .e(simple_display_lower_1_out_5[3]), .d(simple_display_lower_1_out_5[2]),
    .c(simple_display_lower_1_out_5[1]), .dp(simple_display_lower_1_out_5[0]));
  _7_Segment_Display #(.active("false")) u_7_segment_display_38 (
    .g(timer_for_upperr_display_6_out_8[3]), .f(timer_for_upperr_display_6_out_8[2]),
    .a(timer_for_upperr_display_6_out_8[1]), .b(timer_for_upperr_display_6_out_8[0]),
    .e(timer_for_lower_display_6_out_9[3]), .d(timer_for_lower_display_6_out_9[2]),
    .c(timer_for_lower_display_6_out_9[1]), .dp(timer_for_lower_display_6_out_9[0]));
  or or_1 (or_1_out, comparator_1_out_9, comparator_1_out_8);
  _7_Segment_Display #(.active("false")) u_7_segment_display_39 (
    .g(simple_display_upper_1_out_6[3]), .f(simple_display_upper_1_out_6[2]),
    .a(simple_display_upper_1_out_6[1]), .b(simple_display_upper_1_out_6[0]),
    .e(simple_display_lower_1_out_6[3]), .d(simple_display_lower_1_out_6[2]),
    .c(simple_display_lower_1_out_6[1]), .dp(simple_display_lower_1_out_6[0]));
  timer_for_upperr_display timer_for_upperr_display_6 (
    .in_1(button_1_out), .in_2(and_1_out), .out_4(timer_for_upperr_display_6_out_4),
    .out_5(timer_for_upperr_display_6_out_5), .out_6(timer_for_upperr_display_6_out_6),
    .out_7(timer_for_upperr_display_6_out_7), .out_8(timer_for_upperr_display_6_out_8),
    .out_3(timer_for_upperr_display_6_out_3));
  _7_Segment_Display #(.active("false")) u_7_segment_display_40 (
    .g(timer_for_upperr_display_6_out_3[3]), .f(timer_for_upperr_display_6_out_3[2]),
    .a(timer_for_upperr_display_6_out_3[1]), .b(timer_for_upperr_display_6_out_3[0]),
    .e(timer_for_lower_display_6_out_4[3]), .d(timer_for_lower_display_6_out_4[2]),
    .c(timer_for_lower_display_6_out_4[1]), .dp(timer_for_lower_display_6_out_4[0]));
  timer_for_lower_display timer_for_lower_display_6 (
    .out_5(timer_for_lower_display_6_out_5), .out_6(timer_for_lower_display_6_out_6),
    .out_7(timer_for_lower_display_6_out_7), .out_8(timer_for_lower_display_6_out_8),
    .out_9(timer_for_lower_display_6_out_9), .out_4(timer_for_lower_display_6_out_4), .in_1(button_1_out),
    .in_2(and_1_out));  // open: out_3
  _7_Segment_Display #(.active("false")) u_7_segment_display_41 (
    .g(simple_display_upper_1_out_7[3]), .f(simple_display_upper_1_out_7[2]),
    .a(simple_display_upper_1_out_7[1]), .b(simple_display_upper_1_out_7[0]),
    .e(simple_display_lower_1_out_7[3]), .d(simple_display_lower_1_out_7[2]),
    .c(simple_display_lower_1_out_7[1]), .dp(simple_display_lower_1_out_7[0]));
  and and_1 (and_1_out, clock_1_out, not_1_out, START);
  simple_display_upper simple_display_upper_1 (
    .in_1(n16_bit_comparator_1_out_6), .out_3(simple_display_upper_1_out_3),
    .out_4(simple_display_upper_1_out_4), .out_5(simple_display_upper_1_out_5),
    .out_6(simple_display_upper_1_out_6), .out_7(simple_display_upper_1_out_7),
    .out_2(simple_display_upper_1_out_2));
  _7_Segment_Display #(.active("false")) u_7_segment_display_42 (
    .g(simple_display_upper_1_out_2[3]), .f(simple_display_upper_1_out_2[2]),
    .a(simple_display_upper_1_out_2[1]), .b(simple_display_upper_1_out_2[0]),
    .e(simple_display_lower_1_out_2[3]), .d(simple_display_lower_1_out_2[2]),
    .c(simple_display_lower_1_out_2[1]), .dp(simple_display_lower_1_out_2[0]));
  simple_display_lower simple_display_lower_1 (
    .in_1(n16_bit_comparator_1_out_6), .out_3(simple_display_lower_1_out_3),
    .out_4(simple_display_lower_1_out_4), .out_5(simple_display_lower_1_out_5),
    .out_6(simple_display_lower_1_out_6), .out_7(simple_display_lower_1_out_7),
    .out_2(simple_display_lower_1_out_2));
  Clock clock_1 (.out(clock_1_out));
  not not_1 (not_1_out, or_1_out);
  Button button_1 (.out(button_1_out));
  Button button_2 (.out(button_2_out));

  // Notes on the sheet:
  //   RESET
  //   LAP
endmodule

module comparator (
  input  in_1,
  input  in_2,
  output out_3,
  output out_4,
  output out_5,
  output out_6,
  output out_7,
  output out_8,
  output out_9
);

  wire and_1_out, and_4_out, not_1_out, not_2_out;
  wire [2:0] t_ff_1_q;

  T_Flip_Flop t_ff_1 (.clk(in_2), .T(1'b1), .Q(t_ff_1_q[0]), .reset(and_4_out));  // open: Qn, preset, en
  Demultiplexer #(.select(3)) demultiplexer_1 (
    .out0(out_3), .out1(out_4), .out2(out_5), .out3(out_6), .out4(out_7), .in(in_1), .sel(t_ff_1_q), .en(1'b1));  // open: out5, out6, out7
  T_Flip_Flop t_ff_2 (.clk(in_2), .T(t_ff_1_q[0]), .Q(t_ff_1_q[1]), .reset(and_4_out));  // open: Qn, preset, en
  not not_1 (not_1_out, t_ff_1_q[1]);
  T_Flip_Flop t_ff_3 (.clk(in_2), .T(and_1_out), .Q(t_ff_1_q[2]), .reset(and_4_out));  // open: Qn, preset, en
  and and_1 (and_1_out, t_ff_1_q[1], t_ff_1_q[0]);
  and and_2 (out_8, t_ff_1_q[2], t_ff_1_q[1], not_2_out);
  not not_2 (not_2_out, t_ff_1_q[0]);
  and and_3 (out_9, t_ff_1_q[0], not_1_out, t_ff_1_q[2]);
  and and_4 (and_4_out, t_ff_1_q[2], t_ff_1_q[1], t_ff_1_q[0]);
endmodule

module _16_bit_comparator (
  input  [23:0] in_1,
  input  [23:0] in_2,
  input  [23:0] in_3,
  input  [23:0] in_4,
  input  [23:0] in_5,
  output [23:0] out_6
);

  wire [2:0] comparator_1_lt, comparator_2_lt, comparator_3_lt, comparator_4_lt;
  wire [23:0] multiplexer_1_out, multiplexer_2_out, multiplexer_3_out;

  Comparator #(.width(24), .mode("unsigned")) comparator_1 (
    .a(in_1), .b(in_2), .gt(comparator_1_lt[2]), .eq(comparator_1_lt[1]), .lt(comparator_1_lt[0]));
  Comparator #(.width(24), .mode("unsigned")) comparator_2 (
    .a(multiplexer_1_out), .b(in_3), .gt(comparator_2_lt[2]), .eq(comparator_2_lt[1]), .lt(comparator_2_lt[0]));
  Comparator #(.width(24), .mode("unsigned")) comparator_3 (
    .a(multiplexer_2_out), .b(in_4), .gt(comparator_3_lt[2]), .eq(comparator_3_lt[1]), .lt(comparator_3_lt[0]));
  Comparator #(.width(24), .mode("unsigned")) comparator_4 (
    .a(multiplexer_3_out), .b(in_5), .gt(comparator_4_lt[2]), .eq(comparator_4_lt[1]), .lt(comparator_4_lt[0]));
  Multiplexer #(.select(3), .width(24)) multiplexer_1 (
    .in1(in_1), .in2(in_1), .in4(in_2), .out(multiplexer_1_out), .sel(comparator_1_lt), .en(1'b1));  // open: in0, in3, in5, in6, in7
  Multiplexer #(.select(3), .width(24)) multiplexer_2 (
    .in1(multiplexer_1_out), .in2(multiplexer_1_out), .in4(in_3), .out(multiplexer_2_out),
    .sel(comparator_2_lt), .en(1'b1));  // open: in0, in3, in5, in6, in7
  Multiplexer #(.select(3), .width(24)) multiplexer_3 (
    .in1(multiplexer_2_out), .in2(multiplexer_2_out), .in4(in_4), .out(multiplexer_3_out),
    .sel(comparator_3_lt), .en(1'b1));  // open: in0, in3, in5, in6, in7
  Multiplexer #(.select(3), .width(24)) multiplexer_4 (
    .in1(multiplexer_3_out), .in2(multiplexer_3_out), .in4(in_5), .out(out_6), .sel(comparator_4_lt),
    .en(1'b1));  // open: in0, in3, in5, in6, in7
endmodule

module timer (
  input  in_1,
  input  in_2,
  output out_3,
  output out_4,
  output out_5,
  output out_6,
  output out_7,
  output out_8,
  output out_9,
  output out_10,
  output out_11,
  output out_12,
  output out_13,
  output out_14,
  output out_15,
  output out_16,
  output out_17,
  output out_18,
  output out_19,
  output out_20,
  output out_21,
  output out_22,
  output out_23,
  output out_24,
  output out_25,
  output out_26
);

  wire and_1_out, and_2_out, and_3_out, and_4_out, and_5_out, and_6_out, and_7_out, and_8_out, and_9_out,
       and_10_out, not_1_out, not_2_out, not_3_out, not_4_out, not_5_out, not_6_out, not_7_out, not_8_out,
       not_9_out, not_10_out, not_11_out, not_12_out, not_13_out, not_14_out, or_1_out;

  and and_1 (and_1_out, not_1_out, not_2_out, out_5, not_3_out);
  and and_2 (and_2_out, and_1_out, and_4_out);
  not not_1 (not_1_out, out_3);
  not not_2 (not_2_out, out_4);
  mod_10_counter mod_10_counter_1 (
    .in_1(or_1_out), .in_2(and_3_out), .out_3(out_3), .out_4(out_4), .out_5(out_5), .out_6(out_6));
  and and_3 (and_3_out, out_10, not_4_out, not_5_out, out_7);
  not not_3 (not_3_out, out_6);
  and and_4 (and_4_out, not_6_out, out_8, not_8_out, not_7_out);
  not not_4 (not_4_out, out_9);
  not not_5 (not_5_out, out_8);
  not not_6 (not_6_out, out_7);
  and and_5 (and_5_out, and_7_out, and_6_out);
  mod_10_counter mod_10_counter_2 (
    .in_1(or_1_out), .in_2(and_5_out), .out_3(out_7), .out_4(out_8), .out_5(out_9), .out_6(out_10));
  and and_6 (and_6_out, out_14, not_9_out, out_12);
  not not_7 (not_7_out, out_10);
  not not_8 (not_8_out, out_9);
  mod_6_counter mod_6_counter_1 (.in_1(or_1_out), .in_2(and_7_out), .out_3(out_12), .out_4(out_13), .out_5(out_14));
  not not_9 (not_9_out, out_13);
  not not_10 (not_10_out, out_17);
  and and_7 (and_7_out, out_18, not_10_out, not_11_out, out_15);
  not not_11 (not_11_out, out_16);
  and and_8 (and_8_out, and_10_out, and_9_out);
  mod_10_counter mod_10_counter_3 (
    .in_1(or_1_out), .in_2(and_8_out), .out_3(out_15), .out_4(out_16), .out_5(out_17), .out_6(out_18));
  and and_9 (and_9_out, out_22, not_12_out, out_20);
  mod_6_counter mod_6_counter_2 (.in_1(or_1_out), .in_2(and_10_out), .out_3(out_20), .out_4(out_21), .out_5(out_22));
  not not_12 (not_12_out, out_21);
  not not_13 (not_13_out, out_25);
  and and_10 (and_10_out, out_26, not_13_out, not_14_out, out_23);
  not not_14 (not_14_out, out_24);
  or or_1 (or_1_out, in_1, and_2_out);
  mod_10_counter mod_10_counter_4 (
    .in_1(or_1_out), .in_2(in_2), .out_3(out_23), .out_4(out_24), .out_5(out_25), .out_6(out_26));

  assign out_11 = 1'b0;
  assign out_19 = 1'b0;
endmodule

module timer_with_seven_segment_conver (
  input  in_1,
  input  in_2,
  output [6:0] out_3,
  output [6:0] out_4,
  output [6:0] out_5,
  output [6:0] out_6,
  output [6:0] out_7,
  output [6:0] out_8
);

  wire timer_1_out_3, timer_1_out_4, timer_1_out_5, timer_1_out_6, timer_1_out_7, timer_1_out_8,
       timer_1_out_9, timer_1_out_10, timer_1_out_11, timer_1_out_12, timer_1_out_13, timer_1_out_14,
       timer_1_out_15, timer_1_out_16, timer_1_out_17, timer_1_out_18, timer_1_out_19, timer_1_out_20,
       timer_1_out_21, timer_1_out_22, timer_1_out_23, timer_1_out_24, timer_1_out_25, timer_1_out_26;

  bcd_to_seven_segment_decoder bcd_to_seven_segment_decoder_1 (
    .in_1(timer_1_out_3), .in_2(timer_1_out_4), .in_3(timer_1_out_5), .in_4(timer_1_out_6), .out_5(out_4[0]),
    .out_6(out_4[1]), .c(out_4[2]), .out_8(out_4[3]), .out_9(out_4[4]), .out_10(out_4[5]), .out_11(out_4[6]));
  bcd_to_seven_segment_decoder bcd_to_seven_segment_decoder_2 (
    .in_1(timer_1_out_7), .in_2(timer_1_out_8), .in_3(timer_1_out_9), .in_4(timer_1_out_10),
    .out_5(out_5[0]), .out_6(out_5[1]), .c(out_5[2]), .out_8(out_5[3]), .out_9(out_5[4]), .out_10(out_5[5]),
    .out_11(out_5[6]));
  bcd_to_seven_segment_decoder bcd_to_seven_segment_decoder_3 (
    .in_1(timer_1_out_11), .in_2(timer_1_out_12), .in_3(timer_1_out_13), .in_4(timer_1_out_14),
    .out_5(out_6[0]), .out_6(out_6[1]), .c(out_6[2]), .out_8(out_6[3]), .out_9(out_6[4]), .out_10(out_6[5]),
    .out_11(out_6[6]));
  bcd_to_seven_segment_decoder bcd_to_seven_segment_decoder_4 (
    .in_1(timer_1_out_15), .in_2(timer_1_out_16), .in_3(timer_1_out_17), .in_4(timer_1_out_18),
    .out_5(out_7[0]), .out_6(out_7[1]), .c(out_7[2]), .out_8(out_7[3]), .out_9(out_7[4]), .out_10(out_7[5]),
    .out_11(out_7[6]));
  timer timer_1 (
    .in_1(in_1), .in_2(in_2), .out_3(timer_1_out_3), .out_4(timer_1_out_4), .out_5(timer_1_out_5),
    .out_6(timer_1_out_6), .out_7(timer_1_out_7), .out_8(timer_1_out_8), .out_9(timer_1_out_9),
    .out_10(timer_1_out_10), .out_11(timer_1_out_11), .out_12(timer_1_out_12), .out_13(timer_1_out_13),
    .out_14(timer_1_out_14), .out_15(timer_1_out_15), .out_16(timer_1_out_16), .out_17(timer_1_out_17),
    .out_18(timer_1_out_18), .out_19(timer_1_out_19), .out_20(timer_1_out_20), .out_21(timer_1_out_21),
    .out_22(timer_1_out_22), .out_23(timer_1_out_23), .out_24(timer_1_out_24), .out_25(timer_1_out_25),
    .out_26(timer_1_out_26));
  bcd_to_seven_segment_decoder bcd_to_seven_segment_decoder_5 (
    .in_1(timer_1_out_19), .in_2(timer_1_out_20), .in_3(timer_1_out_21), .in_4(timer_1_out_22),
    .out_5(out_8[0]), .out_6(out_8[1]), .c(out_8[2]), .out_8(out_8[3]), .out_9(out_8[4]), .out_10(out_8[5]),
    .out_11(out_8[6]));
  bcd_to_seven_segment_decoder bcd_to_seven_segment_decoder_6 (
    .in_1(timer_1_out_23), .in_2(timer_1_out_24), .in_3(timer_1_out_25), .in_4(timer_1_out_26),
    .out_5(out_3[0]), .out_6(out_3[1]), .c(out_3[2]), .out_8(out_3[3]), .out_9(out_3[4]), .out_10(out_3[5]),
    .out_11(out_3[6]));
endmodule

module timer_for_lower_display (
  input  in_1,
  input  in_2,
  output [23:0] out_3,
  output [3:0] out_4,
  output [3:0] out_5,
  output [3:0] out_6,
  output [3:0] out_7,
  output [3:0] out_8,
  output [3:0] out_9
);

  wire bcd_to_seven_segment_decoder_1_out_5, bcd_to_seven_segment_decoder_1_out_6,
       bcd_to_seven_segment_decoder_1_out_10, bcd_to_seven_segment_decoder_1_out_11,
       bcd_to_seven_segment_decoder_2_out_5, bcd_to_seven_segment_decoder_2_out_6,
       bcd_to_seven_segment_decoder_2_out_10, bcd_to_seven_segment_decoder_2_out_11;

  bcd_to_seven_segment_decoder bcd_to_seven_segment_decoder_1 (
    .in_1(out_3[23]), .in_2(out_3[22]), .in_3(out_3[21]), .in_4(out_3[20]),
    .out_5(bcd_to_seven_segment_decoder_1_out_5), .out_6(bcd_to_seven_segment_decoder_1_out_6), .c(out_5[1]),
    .out_8(out_5[2]), .out_9(out_5[3]), .out_10(bcd_to_seven_segment_decoder_1_out_10),
    .out_11(bcd_to_seven_segment_decoder_1_out_11));
  bcd_to_seven_segment_decoder bcd_to_seven_segment_decoder_2 (
    .in_1(out_3[19]), .in_2(out_3[18]), .in_3(out_3[17]), .in_4(out_3[16]),
    .out_5(bcd_to_seven_segment_decoder_2_out_5), .out_6(bcd_to_seven_segment_decoder_2_out_6), .c(out_6[1]),
    .out_8(out_6[2]), .out_9(out_6[3]), .out_10(bcd_to_seven_segment_decoder_2_out_10),
    .out_11(bcd_to_seven_segment_decoder_2_out_11));
  bcd_to_seven_segment_decoder bcd_to_seven_segment_decoder_3 (
    .in_1(out_3[15]), .in_2(out_3[14]), .in_3(out_3[13]), .in_4(out_3[12]), .c(out_7[1]), .out_8(out_7[2]),
    .out_9(out_7[3]));  // open: out_5, out_6, out_10, out_11
  bcd_to_seven_segment_decoder bcd_to_seven_segment_decoder_4 (
    .in_1(out_3[11]), .in_2(out_3[10]), .in_3(out_3[9]), .in_4(out_3[8]), .c(out_8[1]), .out_8(out_8[2]),
    .out_9(out_8[3]));  // open: out_5, out_6, out_10, out_11
  timer timer_1 (
    .in_1(in_1), .in_2(in_2), .out_3(out_3[23]), .out_4(out_3[22]), .out_5(out_3[21]), .out_6(out_3[20]),
    .out_7(out_3[19]), .out_8(out_3[18]), .out_9(out_3[17]), .out_10(out_3[16]), .out_11(out_3[15]),
    .out_12(out_3[14]), .out_13(out_3[13]), .out_14(out_3[12]), .out_15(out_3[11]), .out_16(out_3[10]),
    .out_17(out_3[9]), .out_18(out_3[8]), .out_19(out_3[7]), .out_20(out_3[6]), .out_21(out_3[5]),
    .out_22(out_3[4]), .out_23(out_3[3]), .out_24(out_3[2]), .out_25(out_3[1]), .out_26(out_3[0]));
  bcd_to_seven_segment_decoder bcd_to_seven_segment_decoder_5 (
    .in_1(out_3[7]), .in_2(out_3[6]), .in_3(out_3[5]), .in_4(out_3[4]), .c(out_9[1]), .out_8(out_9[2]),
    .out_9(out_9[3]));  // open: out_5, out_6, out_10, out_11
  bcd_to_seven_segment_decoder bcd_to_seven_segment_decoder_6 (
    .in_1(out_3[3]), .in_2(out_3[2]), .in_3(out_3[1]), .in_4(out_3[0]), .c(out_4[1]), .out_8(out_4[2]),
    .out_9(out_4[3]));  // open: out_5, out_6, out_10, out_11

  assign out_4[0] = 1'b1;
  assign out_5[0] = 1'b1;
  assign out_6[0] = 1'b1;
  assign out_7[0] = 1'b1;
  assign out_8[0] = 1'b1;
  assign out_9[0] = 1'b1;
endmodule

module timer_for_upperr_display (
  input  in_1,
  input  in_2,
  output [3:0] out_3,
  output [3:0] out_4,
  output [3:0] out_5,
  output [3:0] out_6,
  output [3:0] out_7,
  output [3:0] out_8
);

  wire bcd_to_seven_segment_decoder_1_c, bcd_to_seven_segment_decoder_1_out_8,
       bcd_to_seven_segment_decoder_1_out_9, bcd_to_seven_segment_decoder_2_c,
       bcd_to_seven_segment_decoder_2_out_8, bcd_to_seven_segment_decoder_2_out_9, timer_1_out_3,
       timer_1_out_4, timer_1_out_5, timer_1_out_6, timer_1_out_7, timer_1_out_8, timer_1_out_9,
       timer_1_out_10, timer_1_out_11, timer_1_out_12, timer_1_out_13, timer_1_out_14, timer_1_out_15,
       timer_1_out_16, timer_1_out_17, timer_1_out_18, timer_1_out_19, timer_1_out_20, timer_1_out_21,
       timer_1_out_22, timer_1_out_23, timer_1_out_24, timer_1_out_25, timer_1_out_26;

  bcd_to_seven_segment_decoder bcd_to_seven_segment_decoder_1 (
    .in_1(timer_1_out_3), .in_2(timer_1_out_4), .in_3(timer_1_out_5), .in_4(timer_1_out_6), .out_5(out_4[1]),
    .out_6(out_4[0]), .c(bcd_to_seven_segment_decoder_1_c), .out_8(bcd_to_seven_segment_decoder_1_out_8),
    .out_9(bcd_to_seven_segment_decoder_1_out_9), .out_10(out_4[2]), .out_11(out_4[3]));
  bcd_to_seven_segment_decoder bcd_to_seven_segment_decoder_2 (
    .in_1(timer_1_out_7), .in_2(timer_1_out_8), .in_3(timer_1_out_9), .in_4(timer_1_out_10),
    .out_5(out_5[1]), .out_6(out_5[0]), .c(bcd_to_seven_segment_decoder_2_c),
    .out_8(bcd_to_seven_segment_decoder_2_out_8), .out_9(bcd_to_seven_segment_decoder_2_out_9),
    .out_10(out_5[2]), .out_11(out_5[3]));
  bcd_to_seven_segment_decoder bcd_to_seven_segment_decoder_3 (
    .in_1(timer_1_out_11), .in_2(timer_1_out_12), .in_3(timer_1_out_13), .in_4(timer_1_out_14),
    .out_5(out_6[1]), .out_6(out_6[0]), .out_10(out_6[2]), .out_11(out_6[3]));  // open: c, out_8, out_9
  bcd_to_seven_segment_decoder bcd_to_seven_segment_decoder_4 (
    .in_1(timer_1_out_15), .in_2(timer_1_out_16), .in_3(timer_1_out_17), .in_4(timer_1_out_18),
    .out_5(out_7[1]), .out_6(out_7[0]), .out_10(out_7[2]), .out_11(out_7[3]));  // open: c, out_8, out_9
  timer timer_1 (
    .in_1(in_1), .in_2(in_2), .out_3(timer_1_out_3), .out_4(timer_1_out_4), .out_5(timer_1_out_5),
    .out_6(timer_1_out_6), .out_7(timer_1_out_7), .out_8(timer_1_out_8), .out_9(timer_1_out_9),
    .out_10(timer_1_out_10), .out_11(timer_1_out_11), .out_12(timer_1_out_12), .out_13(timer_1_out_13),
    .out_14(timer_1_out_14), .out_15(timer_1_out_15), .out_16(timer_1_out_16), .out_17(timer_1_out_17),
    .out_18(timer_1_out_18), .out_19(timer_1_out_19), .out_20(timer_1_out_20), .out_21(timer_1_out_21),
    .out_22(timer_1_out_22), .out_23(timer_1_out_23), .out_24(timer_1_out_24), .out_25(timer_1_out_25),
    .out_26(timer_1_out_26));
  bcd_to_seven_segment_decoder bcd_to_seven_segment_decoder_5 (
    .in_1(timer_1_out_19), .in_2(timer_1_out_20), .in_3(timer_1_out_21), .in_4(timer_1_out_22),
    .out_5(out_8[1]), .out_6(out_8[0]), .out_10(out_8[2]), .out_11(out_8[3]));  // open: c, out_8, out_9
  bcd_to_seven_segment_decoder bcd_to_seven_segment_decoder_6 (
    .in_1(timer_1_out_23), .in_2(timer_1_out_24), .in_3(timer_1_out_25), .in_4(timer_1_out_26),
    .out_5(out_3[1]), .out_6(out_3[0]), .out_10(out_3[2]), .out_11(out_3[3]));  // open: c, out_8, out_9
endmodule

module simple_display_upper (
  input  [23:0] in_1,
  output [3:0] out_2,
  output [3:0] out_3,
  output [3:0] out_4,
  output [3:0] out_5,
  output [3:0] out_6,
  output [3:0] out_7
);

  wire bcd_to_seven_segment_decoder_1_c, bcd_to_seven_segment_decoder_1_out_8,
       bcd_to_seven_segment_decoder_1_out_9, bcd_to_seven_segment_decoder_2_c,
       bcd_to_seven_segment_decoder_2_out_8, bcd_to_seven_segment_decoder_2_out_9;

  bcd_to_seven_segment_decoder bcd_to_seven_segment_decoder_1 (
    .in_1(in_1[23]), .in_2(in_1[22]), .in_3(in_1[21]), .in_4(in_1[20]), .out_5(out_3[1]), .out_6(out_3[0]),
    .c(bcd_to_seven_segment_decoder_1_c), .out_8(bcd_to_seven_segment_decoder_1_out_8),
    .out_9(bcd_to_seven_segment_decoder_1_out_9), .out_10(out_3[2]), .out_11(out_3[3]));
  bcd_to_seven_segment_decoder bcd_to_seven_segment_decoder_2 (
    .in_1(in_1[19]), .in_2(in_1[18]), .in_3(in_1[17]), .in_4(in_1[16]), .out_5(out_4[1]), .out_6(out_4[0]),
    .c(bcd_to_seven_segment_decoder_2_c), .out_8(bcd_to_seven_segment_decoder_2_out_8),
    .out_9(bcd_to_seven_segment_decoder_2_out_9), .out_10(out_4[2]), .out_11(out_4[3]));
  bcd_to_seven_segment_decoder bcd_to_seven_segment_decoder_3 (
    .in_1(in_1[15]), .in_2(in_1[14]), .in_3(in_1[13]), .in_4(in_1[12]), .out_5(out_5[1]), .out_6(out_5[0]),
    .out_10(out_5[2]), .out_11(out_5[3]));  // open: c, out_8, out_9
  bcd_to_seven_segment_decoder bcd_to_seven_segment_decoder_4 (
    .in_1(in_1[11]), .in_2(in_1[10]), .in_3(in_1[9]), .in_4(in_1[8]), .out_5(out_6[1]), .out_6(out_6[0]),
    .out_10(out_6[2]), .out_11(out_6[3]));  // open: c, out_8, out_9
  bcd_to_seven_segment_decoder bcd_to_seven_segment_decoder_5 (
    .in_1(in_1[7]), .in_2(in_1[6]), .in_3(in_1[5]), .in_4(in_1[4]), .out_5(out_7[1]), .out_6(out_7[0]),
    .out_10(out_7[2]), .out_11(out_7[3]));  // open: c, out_8, out_9
  bcd_to_seven_segment_decoder bcd_to_seven_segment_decoder_6 (
    .in_1(in_1[3]), .in_2(in_1[2]), .in_3(in_1[1]), .in_4(in_1[0]), .out_5(out_2[1]), .out_6(out_2[0]),
    .out_10(out_2[2]), .out_11(out_2[3]));  // open: c, out_8, out_9
endmodule

module simple_display_lower (
  input  [23:0] in_1,
  output [3:0] out_2,
  output [3:0] out_3,
  output [3:0] out_4,
  output [3:0] out_5,
  output [3:0] out_6,
  output [3:0] out_7
);

  wire bcd_to_seven_segment_decoder_1_out_5, bcd_to_seven_segment_decoder_1_out_6,
       bcd_to_seven_segment_decoder_1_out_10, bcd_to_seven_segment_decoder_1_out_11,
       bcd_to_seven_segment_decoder_2_out_5, bcd_to_seven_segment_decoder_2_out_6,
       bcd_to_seven_segment_decoder_2_out_10, bcd_to_seven_segment_decoder_2_out_11;

  bcd_to_seven_segment_decoder bcd_to_seven_segment_decoder_1 (
    .in_1(in_1[23]), .in_2(in_1[22]), .in_3(in_1[21]), .in_4(in_1[20]),
    .out_5(bcd_to_seven_segment_decoder_1_out_5), .out_6(bcd_to_seven_segment_decoder_1_out_6), .c(out_3[1]),
    .out_8(out_3[2]), .out_9(out_3[3]), .out_10(bcd_to_seven_segment_decoder_1_out_10),
    .out_11(bcd_to_seven_segment_decoder_1_out_11));
  bcd_to_seven_segment_decoder bcd_to_seven_segment_decoder_2 (
    .in_1(in_1[19]), .in_2(in_1[18]), .in_3(in_1[17]), .in_4(in_1[16]),
    .out_5(bcd_to_seven_segment_decoder_2_out_5), .out_6(bcd_to_seven_segment_decoder_2_out_6), .c(out_4[1]),
    .out_8(out_4[2]), .out_9(out_4[3]), .out_10(bcd_to_seven_segment_decoder_2_out_10),
    .out_11(bcd_to_seven_segment_decoder_2_out_11));
  bcd_to_seven_segment_decoder bcd_to_seven_segment_decoder_3 (
    .in_1(in_1[15]), .in_2(in_1[14]), .in_3(in_1[13]), .in_4(in_1[12]), .c(out_5[1]), .out_8(out_5[2]),
    .out_9(out_5[3]));  // open: out_5, out_6, out_10, out_11
  bcd_to_seven_segment_decoder bcd_to_seven_segment_decoder_4 (
    .in_1(in_1[11]), .in_2(in_1[10]), .in_3(in_1[9]), .in_4(in_1[8]), .c(out_6[1]), .out_8(out_6[2]),
    .out_9(out_6[3]));  // open: out_5, out_6, out_10, out_11
  bcd_to_seven_segment_decoder bcd_to_seven_segment_decoder_5 (
    .in_1(in_1[7]), .in_2(in_1[6]), .in_3(in_1[5]), .in_4(in_1[4]), .c(out_7[1]), .out_8(out_7[2]),
    .out_9(out_7[3]));  // open: out_5, out_6, out_10, out_11
  bcd_to_seven_segment_decoder bcd_to_seven_segment_decoder_6 (
    .in_1(in_1[3]), .in_2(in_1[2]), .in_3(in_1[1]), .in_4(in_1[0]), .c(out_2[1]), .out_8(out_2[2]),
    .out_9(out_2[3]));  // open: out_5, out_6, out_10, out_11

  assign out_2[0] = 1'b1;
  assign out_3[0] = 1'b1;
  assign out_4[0] = 1'b1;
  assign out_5[0] = 1'b1;
  assign out_6[0] = 1'b1;
  assign out_7[0] = 1'b1;
endmodule

module useles (
  input  [23:0] in_1,
  input  in_2,
  output out_3,
  output out_4,
  output out_5,
  output out_6,
  output out_7
);

  wire button_1_out;
  wire [3:0] simple_display_lower_1_out_2, simple_display_lower_1_out_3, simple_display_lower_1_out_4,
       simple_display_lower_1_out_5, simple_display_lower_1_out_6, simple_display_lower_1_out_7,
       simple_display_upper_1_out_2, simple_display_upper_1_out_3, simple_display_upper_1_out_4,
       simple_display_upper_1_out_5, simple_display_upper_1_out_6, simple_display_upper_1_out_7;

  Button button_1 (.out(button_1_out));
  comparator comparator_1 (
    .in_1(in_2), .out_3(out_3), .out_4(out_4), .out_5(out_5), .out_6(out_6), .out_7(out_7),
    .in_2(button_1_out));  // open: out_9, out_8
  simple_display_upper simple_display_upper_1 (
    .in_1(in_1), .out_3(simple_display_upper_1_out_3), .out_4(simple_display_upper_1_out_4),
    .out_5(simple_display_upper_1_out_5), .out_6(simple_display_upper_1_out_6),
    .out_7(simple_display_upper_1_out_7), .out_2(simple_display_upper_1_out_2));
  _7_Segment_Display #(.active("false")) u_7_segment_display_1 (
    .g(simple_display_upper_1_out_2[3]), .f(simple_display_upper_1_out_2[2]),
    .a(simple_display_upper_1_out_2[1]), .b(simple_display_upper_1_out_2[0]),
    .e(simple_display_lower_1_out_2[3]), .d(simple_display_lower_1_out_2[2]),
    .c(simple_display_lower_1_out_2[1]), .dp(simple_display_lower_1_out_2[0]));
  simple_display_lower simple_display_lower_1 (
    .in_1(in_1), .out_3(simple_display_lower_1_out_3), .out_4(simple_display_lower_1_out_4),
    .out_5(simple_display_lower_1_out_5), .out_6(simple_display_lower_1_out_6),
    .out_7(simple_display_lower_1_out_7), .out_2(simple_display_lower_1_out_2));
endmodule
